# Fritzing sketch ArduinoUNOR3_télécommande_pour_Thymio_ (saved by Fritzing 0.9.4)
circuit board: 8.46667cm x 5.64444cm
breadboards: 2

parts:
  Part1 = Arduino Uno (Rev3) - ICSP
  R1 = Rotary Potentiometer (Small) [maximum_resistance=1kΩ package=THT]
  Part2 = KY-005 Infrared Transmitter Module [package="Breakout board"]
  S1 = Pushbutton [package="[THT]"]
  S2 = Pushbutton [package="[THT]"]  # not connected
  S3 = Pushbutton [package="[THT]"]
  S4 = Pushbutton [package="[THT]"]
  S5 = Pushbutton [package="[THT]"]
  R2 = Resistor [tolerance=±5% resistance=10k package=THT]
  R3 = Resistor [tolerance=±5% resistance=10k package=THT]
  R4 = Resistor [tolerance=±5% resistance=10k package=THT]
  R5 = Resistor [tolerance=±5% resistance=10k package=THT]

nets:
  N1: Part1.D10_PWM/SS, S5.Pin_3, S5.Pin_4, R5.Pin_1
  N2: Part1.D11_PWM/MOSI, S1.Pin_3, S1.Pin_4, R4.Pin_1
  N3: Part1.D12/MISO, S4.Pin_1, S4.Pin_2, R3.Pin_0
  N4: Part1.D13/SCK, S3.Pin_1, S3.Pin_2, R2.Pin_1
  N5: Part1.D3_PWM, R1.wiper
  N6: Part1.GND, Part2.-
  N7: R1.leg1, Part2.S
  N8: S1.Pin_1, S1.Pin_2, S3.Pin_3, S4.Pin_3, S4.Pin_4, S5.Pin_1, S5.Pin_2
  N9: R2.Pin_0, R3.Pin_1, R4.Pin_0, R5.Pin_0

notes:
  260 Ω
  KY-005 38KHz Infrarouge Sensor
  Module émetteur IR pour Arduino
  ou
  Velleman Vma316 Infrarouge
  Module émetteur pour Arduino
  10k Ω pull down ->

custom parts:
  KY-005 Infrared Transmitter Module: Arduino IR Transmitter Module Keyes KY-005, emits infrared light at 38KHz.
