# Fritzing sketch ArduinoUNOR3_Emetteur_Infrarouge_ (saved by Fritzing 0.9.4)
breadboards: 1

parts:
  Part1 = Arduino Uno (Rev3) - ICSP
  R1 = Rotary Potentiometer (Small) [maximum_resistance=1kΩ package=THT]
  Part2 = KY-005 Infrared Transmitter Module [package="Breakout board"]

nets:
  N1: Part1.D3_PWM, R1.wiper
  N2: Part1.GND, Part2.-
  N3: R1.leg1, Part2.S

notes:
  260 Ω
  KY-005 38KHz Infrarouge Sensor Module émetteur IR pour Arduino
  ou
  Velleman Vma316 Infrarouge Module émetteur pour Arduino

custom parts:
  KY-005 Infrared Transmitter Module: Arduino IR Transmitter Module Keyes KY-005, emits infrared light at 38KHz.
